// Logisim project asdfasf.circ as structural Verilog
module datapath (
  input  clk,
  input  rst_n,
  input  \wire ,
  input  in_4,
  input  sl_1_incd_to_i,
  input  ld_i,
  input  clr_i,
  input  sl_i_minus_1_decrd_to_j,
  input  ld_j,
  input  clr_j,
  input  ld_elem2insert,
  input  clr_elem2insert,
  input  ld_elem2compare,
  input  clr_elem2compare,
  input  sl_i_j_to_arr_ra,
  input  sl_j_j_plus_1_to_arr_wa,
  input  sl_elem2insert_elem2compare_to_arr_w,
  output out_18,
  output out_19,
  output out_20,
  output elem2insert_gt_elem2compare,
  output j_gte_0,
  output i_lt_arr_size
);
endmodule
