// Logisim project datapath.circ as structural Verilog: 1 circuit, main circuit datapath
module datapath (
  input  [3:0] arr_size,
  input  ld_elem2insert,
  input  ld_elem2compare,
  input  ld_j,
  input  sl_decrd_to_j,
  input  ld_i,
  input  sl_incd_to_i,
  input  sl_elem2compare_to_write_data,
  input  sl_j_to_arg_read_addr,
  input  ld_arg_read_addr,
  input  sl_j_plus_1_to_write_addr,
  input  [31:0] r_data,
  input  ld_return_read_data,
  input  clk,
  input  rst_n,
  output elem2insert_gt_elem2compare,
  output [31:0] write_data,
  output j_gte_0,
  output i_lt_arr_size,
  output [3:0] ar_address,
  output [3:0] write_addr
);

  wire comparator_2_lt, reset;
  wire [4:0] adder_1_out, i, j, multiplexer_1_out, multiplexer_2_out, multiplexer_3_out, subtractor_1_out;
  wire [4:4] adder_2_out;
  wire [31:0] elem2compare_q, elem2ins, q_read_return_data;

  not not_1 (reset, rst_n);
  Multiplexer #(.width(5)) multiplexer_1 (
    .in0(5'b00001), .in1(adder_1_out), .out(multiplexer_1_out), .sel(sl_incd_to_i));
  Adder #(.width(5)) adder_1 (.a(5'b00001), .b(i), .out(adder_1_out), .cin(1'b0));  // open: cout
  Multiplexer #(.width(5)) multiplexer_2 (.in0(i), .in1(j), .out(multiplexer_2_out), .sel(sl_j_to_arg_read_addr));
  Register #(.width(5)) u_i (.D(multiplexer_1_out), .en(ld_i), .clk(clk), .Q(i), .clr(reset));
  Register #(.width(4)) arg_read_addr (
    .D(multiplexer_2_out[3:0]), .en(ld_arg_read_addr), .clk(clk), .Q(ar_address), .clr(reset));
  Register #(.width(32)) elem2insert (
    .D(q_read_return_data), .en(ld_elem2insert), .clk(clk), .Q(elem2ins), .clr(reset));
  Multiplexer #(.width(5)) multiplexer_3 (.in0(i), .in1(j), .out(multiplexer_3_out), .sel(sl_decrd_to_j));
  Register #(.width(5)) u_j (.D(subtractor_1_out), .en(ld_j), .clk(clk), .Q(j), .clr(reset));
  Subtractor #(.width(5)) subtractor_1 (
    .a(multiplexer_3_out), .b(5'b00001), .out(subtractor_1_out), .bin(1'b0));  // open: bout
  Adder #(.width(5)) adder_2 (
    .a(j), .b({5{1'b0}}), .out({adder_2_out[4], write_addr}), .cin(sl_j_plus_1_to_write_addr));  // open: cout
  Register #(.width(32)) elem2compare (
    .D(q_read_return_data), .en(ld_elem2compare), .clk(clk), .Q(elem2compare_q), .clr(reset));
  Register #(.width(32)) read_return_data (
    .D(r_data), .en(ld_return_read_data), .clk(clk), .Q(q_read_return_data), .clr(reset));
  Comparator #(.width(32)) comparator_1 (
    .a(elem2ins), .b(elem2compare_q), .gt(elem2insert_gt_elem2compare));  // open: eq, lt
  Multiplexer #(.width(32)) multiplexer_4 (
    .in0(elem2ins), .in1(elem2compare_q), .out(write_data), .sel(sl_elem2compare_to_write_data));
  Comparator #(.width(5)) comparator_2 (.a(j), .b({5{1'b0}}), .lt(comparator_2_lt));  // open: gt, eq
  not not_2 (j_gte_0, comparator_2_lt);
  Comparator #(.width(5)) comparator_3 (.a({1'b0, arr_size}), .b(i), .gt(i_lt_arr_size));  // open: eq, lt

  // Other names for the same wires on the sheet: d_read_return_data[31:0] = r_data
endmodule
