// Logisim project memory.circ as structural Verilog: 1 circuit, main circuit memory
module memory (
  input  clk,
  input  rst_n,
  input  ar_valid,
  input  [3:0] ar_address,
  input  aw_valid,
  input  [3:0] aw_address,
  input  r_ready,
  input  [31:0] w_data,
  input  w_valid,
  input  b_ready,
  output aw_ready,
  output ar_ready,
  output [31:0] r_data,
  output w_ready,
  output r_valid,
  output r_resp,
  output b_valid,
  output b_resp
);

  wire reset;
  wire [3:0] multiplexer_1_out;

  not not_1 (reset, rst_n);
  Multiplexer #(.width(4)) multiplexer_1 (.in0(ar_address), .in1(aw_address), .out(multiplexer_1_out), .sel(1'b0));
  RAM #(.addrWidth(4), .dataWidth(32)) ram_1 (
    .addr(multiplexer_1_out), .we(1'b0), .oe(1'b1), .clk(clk), .din(w_data), .dout(r_data));
endmodule
